// Digital circuit TIPO J.dig as structural Verilog
module TIPO_J (
  input  [31:0] Inst,
  output [6:0] Opcode,
  output [4:0] Rd,
  output [31:0] ImmJ
);

  BitExtender #(.inputBits(1), .outputBits(11)) bitextender_1 (.in(Inst[31]), .out(ImmJ[31:21]));

  assign ImmJ[20:0] = {Inst[31], Inst[19:12], Inst[20], Inst[30:21], 1'b0};
  assign Opcode = Inst[6:0];
  assign Rd = Inst[11:7];
endmodule
