// Digital circuit TIPO R.dig as structural Verilog
module TIPO_R (
  input  [31:0] Inst,
  output [6:0] Opcode,
  output [4:0] Rd,
  output [2:0] Funct3,
  output [4:0] Rs1,
  output [4:0] Rs2,
  output [6:0] Func7
);


  assign Func7 = Inst[31:25];
  assign Funct3 = Inst[14:12];
  assign Opcode = Inst[6:0];
  assign Rd = Inst[11:7];
  assign Rs1 = Inst[19:15];
  assign Rs2 = Inst[24:20];
endmodule
