// Digital circuit TIPO S.dig as structural Verilog
module TIPO_S (
  input  [31:0] Inst,
  output [6:0] Opcode,
  output [2:0] Funct3,
  output [4:0] Rs1,
  output [4:0] Rs2,
  output [31:0] ImmS
);

  BitExtender #(.inputBits(1), .outputBits(20)) bitextender_1 (.in(Inst[20]), .out(ImmS[31:12]));
  // Pins of 1 and 12 bits meet at Inst[31:20]

  assign Funct3 = Inst[14:12];
  assign ImmS[11:0] = {Inst[31:25], Inst[11:7]};
  assign Opcode = Inst[6:0];
  assign Rs1 = Inst[19:15];
  assign Rs2 = Inst[24:20];
endmodule
