// Digital circuit Prototipo.dig as structural Verilog
module Prototipo (
  input  [31:0] Inst,
  output [6:0] Opcode,
  output [4:0] Rd,
  output [2:0] Funct3,
  output [4:0] Rs1,
  output [4:0] Rs2,
  output [6:0] Func7,
  output [31:0] lmm,
  output [4:0] Sham__i,
  output Srai_Srli,
  output [31:0] ImmS,
  output [31:0] ImmB
);

  BitExtender #(.inputBits(1), .outputBits(20)) bitextender_1 (.in(Inst[31]), .out(ImmS[31:12]));

  assign Func7 = Inst[31:25];
  assign Funct3 = Inst[14:12];
  assign ImmS[11:0] = {Inst[31:25], Inst[11:7]};
  assign lmm = {ImmS[31:12], Inst[31:20]};
  assign Opcode = Inst[6:0];
  assign Rd = Inst[11:7];
  assign Rs1 = Inst[19:15];
  assign Rs2 = Inst[24:20];
  assign Sham__i = Inst[24:20];
  assign Srai_Srli = Inst[30];
endmodule
