// Digital circuit TIPO B.dig as structural Verilog
module TIPO_B (
  input  [31:0] Inst,
  output [6:0] Opcode,
  output [2:0] Funct3,
  output [4:0] Rs1,
  output [4:0] Rs2,
  output [12:0] ImmB
);


  assign Funct3 = Inst[14:12];
  assign ImmB = {Inst[31], Inst[7], Inst[30:25], Inst[11:8], 1'b0};
  assign Opcode = Inst[6:0];
  assign Rs1 = Inst[19:15];
  assign Rs2 = Inst[24:20];
endmodule
